// Logisim project Relogio.circ as structural Verilog: 2 circuits, main circuit main
module main (
);

  wire and_1_out, clock_1_out;
  wire [5:0] t_ff_1_q;

  Clock clock_1 (.out(clock_1_out));
  T_Flip_Flop #(.trigger("falling")) t_ff_1 (
    .clk(clock_1_out), .T(1'b1), .Q(t_ff_1_q[0]), .reset(and_1_out));  // open: Qn, preset, en
  and and_1 (and_1_out, t_ff_1_q[5], t_ff_1_q[4], t_ff_1_q[3], t_ff_1_q[2], ~t_ff_1_q[1], ~t_ff_1_q[0]);  // AND_Gate
  // Probe on t_ff_1_q
  T_Flip_Flop #(.trigger("falling")) t_ff_2 (
    .clk(t_ff_1_q[0]), .T(1'b1), .Q(t_ff_1_q[1]), .reset(and_1_out));  // open: Qn, preset, en
  T_Flip_Flop #(.trigger("falling")) t_ff_3 (
    .clk(t_ff_1_q[1]), .T(1'b1), .Q(t_ff_1_q[2]), .reset(and_1_out));  // open: Qn, preset, en
  T_Flip_Flop #(.trigger("falling")) t_ff_4 (
    .clk(t_ff_1_q[2]), .T(1'b1), .Q(t_ff_1_q[3]), .reset(and_1_out));  // open: Qn, preset, en
  T_Flip_Flop #(.trigger("falling")) t_ff_5 (
    .clk(t_ff_1_q[3]), .T(1'b1), .Q(t_ff_1_q[4]), .reset(and_1_out));  // open: Qn, preset, en
  T_Flip_Flop #(.trigger("falling")) t_ff_6 (
    .clk(t_ff_1_q[4]), .T(1'b1), .Q(t_ff_1_q[5]), .reset(and_1_out));  // open: Qn, preset, en
endmodule

module relogio (
);

  wire clock_1_out, clock_2_out, t_ff_5_q, t_ff_6_q, t_ff_8_q, undriven, undriven_2;
  wire [3:0] t_ff_1_q;

  Clock clock_1 (.out(clock_1_out));
  T_Flip_Flop #(.trigger("falling")) t_ff_1 (
    .clk(clock_1_out), .T(1'b1), .Q(t_ff_1_q[0]), .reset(undriven));  // open: Qn, preset, en
  T_Flip_Flop #(.trigger("falling")) t_ff_2 (
    .clk(t_ff_1_q[0]), .T(1'b1), .Q(t_ff_1_q[1]), .reset(undriven));  // open: Qn, preset, en
  T_Flip_Flop #(.trigger("falling")) t_ff_3 (
    .clk(t_ff_1_q[1]), .T(1'b1), .Q(t_ff_1_q[2]), .reset(undriven));  // open: Qn, preset, en
  T_Flip_Flop #(.trigger("falling")) t_ff_4 (
    .clk(t_ff_1_q[2]), .T(1'b1), .Q(t_ff_1_q[3]), .reset(undriven));  // open: Qn, preset, en
  Clock clock_2 (.out(clock_2_out));
  T_Flip_Flop #(.trigger("falling")) t_ff_5 (
    .clk(clock_2_out), .T(1'b1), .Q(t_ff_5_q), .reset(undriven_2));  // open: Qn, preset, en
  T_Flip_Flop #(.trigger("falling")) t_ff_6 (
    .clk(t_ff_5_q), .T(1'b1), .Q(t_ff_6_q), .reset(undriven_2));  // open: Qn, preset, en
  T_Flip_Flop #(.trigger("falling")) t_ff_7 (.clk(t_ff_8_q), .T(1'b1), .reset(undriven_2));  // open: Q, Qn, preset, en
  T_Flip_Flop #(.trigger("falling")) t_ff_8 (
    .clk(t_ff_6_q), .T(1'b1), .Q(t_ff_8_q), .reset(undriven_2));  // open: Qn, preset, en
endmodule
